# Fritzing sketch Yun_PackageDetection (saved by Fritzing 0.8.5b)
circuit board: 8.46667cm x 5.64444cm
breadboards: 1

parts:
  J1 = Basic Force Sensing Resistor (FSR) [package=THT]
  Part1 = Arduino Yun
  R1 = Resistor [tolerance=±5% resistance=10k package=THT]

nets:
  N1: J1.pin_0, Part1.5V
  N2: J1.pin_1, Part1.A0, R1.Pin_0
  N3: Part1.GND, R1.Pin_1

notes:
  Yun PDNS
  (C) 2014 Green Shoe Garage
  Design v1.0
  Production Lot 18JAN2014

custom parts:
  Arduino Yun: The new Arduino Yun is a microcontroller board based on the ATmega32u4 (datasheet) and the Atheros AR9331. The Atheros processor supports a Linux distribution based on OpenWRT named Linino. The board has built-in Ethernet and WiFi support, a USB-A port, micro-SD card slot, 20 digital input/output pins (of which 7 can be used as PWM outputs and 12 as analog inputs), a 16 MHz crystal oscillator,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
